// Digital circuit adder4b.dig as structural Verilog
module adder4b (
  input  A0,
  input  A1,
  input  A2,
  input  A3,
  input  B0,
  input  B1,
  input  B2,
  input  B3,
  input  Ci,
  output S0,
  output S1,
  output S2,
  output S3,
  output Co
);

  wire fulladder_2_co, fulladder_3_co, fulladder_4_co;

  fulladder fulladder_1 (.S(S3), .Co(Co), .A(A3), .B(B3), .Ci(fulladder_2_co));
  fulladder fulladder_2 (.S(S2), .Co(fulladder_2_co), .A(A2), .B(B2), .Ci(fulladder_3_co));
  fulladder fulladder_3 (.S(S1), .Co(fulladder_3_co), .A(A1), .B(B1), .Ci(fulladder_4_co));
  fulladder fulladder_4 (.S(S0), .Co(fulladder_4_co), .A(A0), .B(B0), .Ci(Ci));
endmodule
