// Digital circuit addsub4b.dig as structural Verilog
module addsub4b (
  input  A0,
  input  A1,
  input  A2,
  input  A3,
  input  B0,
  input  B1,
  input  B2,
  input  B3,
  input  add__sub,
  output R0,
  output R1,
  output R2,
  output R3,
  output Co
);

  wire xor_1_out, xor_2_out, xor_3_out, xor_4_out;

  xor xor_1 (xor_1_out, B0, add__sub);
  xor xor_2 (xor_2_out, B1, add__sub);
  xor xor_3 (xor_3_out, B2, add__sub);
  xor xor_4 (xor_4_out, B3, add__sub);
  adder4b adder4b_1 (
    .A0(A0), .A1(A1), .A2(A2), .A3(A3), .B0(xor_1_out), .B1(xor_2_out), .B2(xor_3_out), .B3(xor_4_out),
    .Ci(add__sub), .S0(R0), .S1(R1), .S2(R2), .S3(R3), .Co(Co));

  // Notes on the sheet:
  //   addsub4b - Somador/subtrator de 4 bits
  //   (add\_sub=0 => add; add\_sub=1 => sub)
endmodule
