// Digital circuit fulladder.dig as structural Verilog
module fulladder (
  input  A,
  input  Ci,
  input  B,
  output S,
  output Co
);

  sum sum_1 (.A(A), .B(B), .Ci(Ci), .S(S));
  carryout carryout_1 (.A(A), .B(B), .Ci(Ci), .Co(Co));
endmodule
