// Digital circuit ALU.dig as structural Verilog
module ALU (
  input  [7:0] A,
  input  [7:0] B,
  input  [2:0] OPR,
  output [7:0] R,
  output [3:0] FLAGS
);

  wire opalu_1_co;

  opALU opalu_1 (.A(A), .B(B), .OPR(OPR), .R(R), .Co(opalu_1_co));
  flags flags_1 (.OPR(OPR), .sA(A[7]), .sB(B[7]), .R(R), .Co(opalu_1_co), .FLAGS(FLAGS));

  // Notes on the sheet:
  //   OPR   Valor de R (significado)
  //   -----------------------------------------------
  //   000    B (saída é igual à entrada B)
  //   001      A - B (diferença entre A e B)
  //   010      A + B (soma de A e B)
  //   011  A ^ B (ou-exclusivo entre A e B)
  //   100      A >> 1 (quociente da divisão de A por 2)
  //   101      A << 1 (multiplicação de A por 2)
  //   110      A & B (e-lógico entre os bits de A e B)
  //   111      A | B    (ou-lógico entre os bits de A e B)
endmodule
