// Digital circuit ALUregs_IO.dig as structural Verilog
module ALUregs_IO (
  input  [7:0] B,
  input  [2:0] OPR
);

  wire clk_out;
  wire [3:0] alu_1_flags, REG4_q, REG8_q;
  wire [7:0] alu_1_r;
  wire [7:4] REG8_q_2;

  Button clk (.out(clk_out));
  ALU alu_1 (.A({REG8_q_2, REG8_q}), .B(B), .OPR(OPR), .R(alu_1_r), .FLAGS(alu_1_flags));
  D_FF #(.Bits(8)) REG8 (.D(alu_1_r), .C(clk_out), .Q({REG8_q_2, REG8_q}));  // open: nQ
  D_FF #(.Bits(4)) REG4 (.D(alu_1_flags), .C(clk_out), .Q(REG4_q));  // open: nQ
  Seven_Seg_Hex seven_seg_hex_1 (.d(alu_1_r[7:4]), .dp(1'b0));
  Seven_Seg_Hex seven_seg_hex_2 (.d(alu_1_r[3:0]), .dp(1'b0));
  LED led_1 (.in(REG4_q[3]));
  Seven_Seg_Hex seven_seg_hex_3 (.d(REG8_q_2), .dp(1'b0));
  LED led_2 (.in(REG4_q[2]));
  LED led_3 (.in(REG4_q[1]));
  Seven_Seg_Hex seven_seg_hex_4 (.d(REG8_q), .dp(1'b0));
  LED led_4 (.in(REG4_q[0]));
  Seven_Seg_Hex seven_seg_hex_5 (.d(B[7:4]), .dp(1'b0));
  Seven_Seg_Hex seven_seg_hex_6 (.d(B[3:0]), .dp(1'b0));

  // Notes on the sheet:
  //   R
  //   O
  //   A
  //   C
  //   S
  //   Z
  //   B
endmodule
