// Digital circuit AS.dig as structural Verilog
module AS (
  input  O0,
  input  O1,
  input  O2,
  output AS
);

  wire and_1_out, and_2_out, not_1_out, not_2_out, not_3_out;

  not not_1 (not_1_out, O2);
  not not_2 (not_2_out, O1);
  not not_3 (not_3_out, O0);
  and and_1 (and_1_out, O0, not_2_out, not_1_out);
  and and_2 (and_2_out, not_3_out, O1, not_1_out);
  or or_1 (AS, and_1_out, and_2_out);

  // Notes on the sheet:
  //   Obtido por síntese a partir da tabela de verdade (AS.tru)
endmodule
