// Digital circuit DEC2_4.dig as structural Verilog
module DEC2_4 (
  input  [1:0] CE,
  input  en,
  output Y0,
  output Y1,
  output Y2,
  output Y3
);

  wire decoder_1_out_0, decoder_1_out_1, decoder_1_out_2, decoder_1_out_3;

  Decoder #(.Selector_Bits(2)) decoder_1 (
    .sel(CE), .out_0(decoder_1_out_0), .out_1(decoder_1_out_1), .out_2(decoder_1_out_2),
    .out_3(decoder_1_out_3));
  and and_1 (Y0, decoder_1_out_0, en);
  and and_2 (Y1, decoder_1_out_1, en);
  and and_3 (Y2, decoder_1_out_2, en);
  and and_4 (Y3, decoder_1_out_3, en);

  // Notes on the sheet:
  //   Descodificador de 2 para 4 com enable
endmodule
