// Digital circuit addsub4b_IO.dig as structural Verilog
module addsub4b_IO (
  input  B0,
  input  B1,
  input  B2,
  input  B3,
  input  A3,
  input  A2,
  input  A1,
  input  A0
);

  wire add__sub_out;
  wire [0:0] addsub4b_1_co;
  wire [3:0] addsub4b_1_r3;

  Button add__sub (.out(add__sub_out));
  addsub4b addsub4b_1 (
    .A0(A0), .A1(A1), .A2(A2), .A3(A3), .B0(B0), .B1(B1), .B2(B2), .B3(B3), .add__sub(add__sub_out),
    .R0(addsub4b_1_r3[0]), .R1(addsub4b_1_r3[1]), .R2(addsub4b_1_r3[2]), .R3(addsub4b_1_r3[3]),
    .Co(addsub4b_1_co[0]));
  Seven_Seg_Hex seven_seg_hex_1 (.d({3'b000, addsub4b_1_co[0]}), .dp(1'b0));
  Seven_Seg_Hex seven_seg_hex_2 (.d(addsub4b_1_r3), .dp(1'b0));
  Seven_Seg_Hex seven_seg_hex_3 (.d({A3, A2, A1, A0}), .dp(1'b0));
  Seven_Seg_Hex seven_seg_hex_4 (.d({B3, B2, B1, B0}), .dp(1'b0));

  // Notes on the sheet:
  //   addsub4b - Somador/subtrator de 4 bits com I/O
  //   (add\_sub=0 => add; add\_sub=1 => sub)
  //   Co
  //   R
  //   A
  //   B
endmodule
