// Digital circuit carryout.dig as structural Verilog
module carryout (
  input  A,
  input  B,
  input  Ci,
  output Co
);

  wire and_1_out, and_2_out, and_3_out;

  and and_1 (and_1_out, A, B);
  and and_2 (and_2_out, B, Ci);
  and and_3 (and_3_out, A, Ci);
  or or_1 (Co, and_1_out, and_2_out, and_3_out);
endmodule
