// Digital circuit sum.dig as structural Verilog
module sum (
  input  A,
  input  B,
  input  Ci,
  output S
);

  wire xor_1_out;

  xor xor_1 (xor_1_out, A, B);
  xor xor_2 (S, xor_1_out, Ci);
endmodule
