// Digital circuit OV.dig as structural Verilog
module OV (
  input  O0,
  input  sA,
  input  sB,
  input  sR,
  output OV
);

  wire and_1_out, and_2_out, and_3_out, and_4_out, not_1_out, not_2_out, not_3_out, not_4_out;

  not not_1 (not_1_out, O0);
  not not_2 (not_2_out, sA);
  not not_3 (not_3_out, sB);
  not not_4 (not_4_out, sR);
  and and_1 (and_1_out, not_1_out, not_2_out, not_3_out, sR);
  and and_2 (and_2_out, not_1_out, sA, sB, not_4_out);
  and and_3 (and_3_out, O0, not_2_out, sB, sR);
  and and_4 (and_4_out, O0, sA, not_3_out, not_4_out);
  or or_1 (OV, and_1_out, and_2_out, and_3_out, and_4_out);

  // Notes on the sheet:
  //   Obtido por síntese a partir da tabela de verdade (OV.tru)
endmodule
