// Digital circuit REG4er.dig as structural Verilog
module REG4er (
  input  [3:0] D,
  input  en,
  input  rst,
  input  clk,
  output [3:0] Q
);

  wire [3:0] multiplexer_1_out;

  Multiplexer #(.Bits(4)) multiplexer_1 (.sel(en), .in_0(Q), .in_1(D), .out(multiplexer_1_out));
  D_FF_AS #(.Bits(4)) REG4rst (.Set(1'b0), .D(multiplexer_1_out), .C(clk), .Clr(rst), .Q(Q));  // open: nQ

  // Notes on the sheet:
  //   Registo de 4 bits com enable e reset assíncrono
endmodule
