// Digital circuit REG8er.dig as structural Verilog
module REG8er (
  input  [7:0] D,
  input  en,
  input  rst,
  input  clk,
  output [7:0] Q
);

  wire [7:0] multiplexer_1_out;

  Multiplexer #(.Bits(8)) multiplexer_1 (.sel(en), .in_0(Q), .in_1(D), .out(multiplexer_1_out));
  D_FF_AS #(.Bits(8)) REG8rst (.Set(1'b0), .D(multiplexer_1_out), .C(clk), .Clr(rst), .Q(Q));  // open: nQ

  // Notes on the sheet:
  //   Registo de 8 bits com enable e reset assíncrono
endmodule
