// Digital circuit add8.dig as structural Verilog
module add8 (
  input  [7:0] A,
  input  [7:0] B,
  output [7:0] R,
  output Co
);

  wire adder4b_1_co;

  adder4b adder4b_1 (
    .A0(A[0]), .A1(A[1]), .A2(A[2]), .A3(A[3]), .B0(B[0]), .B1(B[1]), .B2(B[2]), .B3(B[3]), .Ci(1'b0),
    .S0(R[0]), .S1(R[1]), .S2(R[2]), .S3(R[3]), .Co(adder4b_1_co));
  adder4b adder4b_2 (
    .A0(A[4]), .A1(A[5]), .A2(A[6]), .A3(A[7]), .B0(B[4]), .B1(B[5]), .B2(B[6]), .B3(B[7]),
    .Ci(adder4b_1_co), .S0(R[4]), .S1(R[5]), .S2(R[6]), .S3(R[7]), .Co(Co));
endmodule
