// Digital circuit datapath_IO.dig as structural Verilog
module datapath_IO (
  input  [7:0] X,
  input  [2:0] OPR,
  input  [2:0] SEL,
  input  [1:0] CE,
  input  reset,
  input  in_6
);

  wire clk_out, dec2_4_1_y0, dec2_4_1_y1, dec2_4_1_y2, dec2_4_1_y3;
  wire [3:0] alu_1_flags, alu_1_r, alu_1_r_2, FLAGS_q;
  wire [7:0] A_q, multiplexer_1_out, R1_q, R2_q, R3_q;

  Button clk (.out(clk_out));
  DEC2_4 dec2_4_1 (.CE(CE), .en(in_6), .Y0(dec2_4_1_y0), .Y1(dec2_4_1_y1), .Y2(dec2_4_1_y2), .Y3(dec2_4_1_y3));
  REG8er A (.D({alu_1_r_2, alu_1_r}), .en(dec2_4_1_y0), .rst(reset), .clk(clk_out), .Q(A_q));
  REG8er R1 (.D({alu_1_r_2, alu_1_r}), .en(dec2_4_1_y1), .rst(reset), .clk(clk_out), .Q(R1_q));
  REG8er R2 (.D({alu_1_r_2, alu_1_r}), .en(dec2_4_1_y2), .rst(reset), .clk(clk_out), .Q(R2_q));
  REG8er R3 (.D({alu_1_r_2, alu_1_r}), .en(dec2_4_1_y3), .rst(reset), .clk(clk_out), .Q(R3_q));
  Multiplexer #(.Selector_Bits(3), .Bits(8)) multiplexer_1 (
    .sel(SEL), .in_0(A_q), .in_1(R1_q), .in_2(R2_q), .in_3(R3_q), .in_4(X), .in_5(8'h1), .in_6(8'hf),
    .in_7({{7{1'b0}}, FLAGS_q[2]}), .out(multiplexer_1_out));
  ALU alu_1 (.A(A_q), .B(multiplexer_1_out), .OPR(OPR), .R({alu_1_r_2, alu_1_r}), .FLAGS(alu_1_flags));
  REG4er FLAGS (.D(alu_1_flags), .en(1'b1), .rst(reset), .clk(clk_out), .Q(FLAGS_q));
  Seven_Seg_Hex seven_seg_hex_1 (.d(alu_1_r_2), .dp(1'b0));
  Seven_Seg_Hex seven_seg_hex_2 (.d(alu_1_r), .dp(1'b0));
  Seven_Seg_Hex seven_seg_hex_3 (.d(A_q[7:4]), .dp(1'b0));
  Seven_Seg_Hex seven_seg_hex_4 (.d(A_q[3:0]), .dp(1'b0));
  LED led_1 (.in(FLAGS_q[3]));
  LED led_2 (.in(FLAGS_q[2]));
  LED led_3 (.in(FLAGS_q[1]));
  Seven_Seg_Hex seven_seg_hex_5 (.d(multiplexer_1_out[7:4]), .dp(1'b0));
  LED led_4 (.in(FLAGS_q[0]));
  Seven_Seg_Hex seven_seg_hex_6 (.d(multiplexer_1_out[3:0]), .dp(1'b0));

  // Notes on the sheet:
  //   C
  //   Circuito incompleto !!!
  //   R
  //   A
  //   O
  //   S
  //   B
  //   Z
endmodule
