// Digital circuit flags.dig as structural Verilog
// Circuito que define o valor das flags.
module flags (
  input  [2:0] OPR,
  input  sA,
  input  sB,
  input  [7:0] R,
  input  Co,
  output [3:0] FLAGS
);

  wire as_1_as, or_1_out, or_2_out, ov_1_ov;

  or or_1 (or_1_out, R[0], R[1], R[2], R[3]);
  or or_2 (or_2_out, R[4], R[5], R[6], R[7]);
  AS as_1 (.O0(OPR[0]), .O1(OPR[1]), .O2(OPR[2]), .AS(as_1_as));
  OV ov_1 (.O0(OPR[0]), .sA(sA), .sB(sB), .sR(R[7]), .OV(ov_1_ov));
  nor nor_1 (FLAGS[0], or_1_out, or_2_out);
  and and_1 (FLAGS[2], Co, as_1_as);
  and and_2 (FLAGS[3], as_1_as, ov_1_ov);

  assign FLAGS[1] = R[7];

  // Notes on the sheet:
  //   ZERO
  //   SINAL
  //   CARRY
  //   OVFL
endmodule
