// Digital circuit opALU.dig as structural Verilog
module opALU (
  input  [7:0] A,
  input  [7:0] B,
  input  [2:0] OPR,
  output [7:0] R,
  output Co
);

  wire add8_1_co, sub8_1_co;
  wire [7:0] add8_1_r, and8_1_r, or8_1_r, sar_1_r, sll_1_r, sub8_1_r, xor8_1_r;

  sub8 sub8_1 (.A(A), .B(B), .R(sub8_1_r), .Co(sub8_1_co));
  add8 add8_1 (.A(A), .B(B), .R(add8_1_r), .Co(add8_1_co));
  xor8 xor8_1 (.A(A), .B(B), .R(xor8_1_r));
  SAR sar_1 (.A(A), .R(sar_1_r));
  SLL sll_1 (.A(A), .R(sll_1_r));
  and8 and8_1 (.A(A), .B(B), .R(and8_1_r));
  or8 or8_1 (.A(A), .B(B), .R(or8_1_r));
  Multiplexer #(.Selector_Bits(3)) multiplexer_1 (
    .sel(OPR), .in_0(1'b0), .in_1(sub8_1_co), .in_2(add8_1_co), .in_3(1'b0), .in_4(1'b0), .in_5(1'b0),
    .in_6(1'b0), .in_7(1'b0), .out(Co));
  Multiplexer #(.Selector_Bits(3), .Bits(8)) multiplexer_2 (
    .sel(OPR), .in_0(B), .in_1(sub8_1_r), .in_2(add8_1_r), .in_3(xor8_1_r), .in_4(sar_1_r), .in_5(sll_1_r),
    .in_6(and8_1_r), .in_7(or8_1_r), .out(R));

  // Notes on the sheet:
  //   OPR: OPR    R
  //   000      B
  //   001   A - B
  //   010   A + B
  //   011   A ^ B
  //   100   A >> 1
  //   101   A << 1
  //   110   A & B
  //   111   A | B
endmodule
