// Digital circuit sub8.dig as structural Verilog
module sub8 (
  input  [7:0] A,
  input  [7:0] B,
  output [7:0] R,
  output Co
);

  wire adder4b_1_co, not_1_out, not_2_out, not_3_out, not_4_out, not_5_out, not_6_out, not_7_out, not_8_out;

  not not_1 (not_1_out, B[0]);
  not not_2 (not_2_out, B[2]);
  not not_3 (not_3_out, B[4]);
  not not_4 (not_4_out, B[6]);
  not not_5 (not_5_out, B[1]);
  not not_6 (not_6_out, B[3]);
  not not_7 (not_7_out, B[5]);
  not not_8 (not_8_out, B[7]);
  adder4b adder4b_1 (
    .A0(A[0]), .A1(A[1]), .A2(A[2]), .A3(A[3]), .B0(not_1_out), .B1(not_5_out), .B2(not_2_out),
    .B3(not_6_out), .Ci(1'b1), .S0(R[0]), .S1(R[1]), .S2(R[2]), .S3(R[3]), .Co(adder4b_1_co));
  adder4b adder4b_2 (
    .A0(A[4]), .A1(A[5]), .A2(A[6]), .A3(A[7]), .B0(not_3_out), .B1(not_7_out), .B2(not_4_out),
    .B3(not_8_out), .Ci(adder4b_1_co), .S0(R[4]), .S1(R[5]), .S2(R[6]), .S3(R[7]), .Co(Co));

  // Notes on the sheet:
  //   A - B = A + (- B) = A + (B' + 1)
endmodule
